// Digital circuit CPU.dig as structural Verilog
module CPU (
  input  I0,
  input  I1,
  input  I2,
  input  I3,
  input  I4,
  input  I5,
  input  I6,
  input  I7,
  input  WRegB,
  input  WRegA,
  input  Sum_Substract,
  input  in_24,
  input  in_25,
  input  in_26,
  output Negative,
  output Carry_out,
  output Zero,
  output Overflow,
  output Y0,
  output Y1,
  output Y2,
  output Y3,
  output Y4,
  output Y5,
  output Y6,
  output Y7
);

  wire flipflop_8bit_1_p1, flipflop_8bit_1_p2, flipflop_8bit_1_p3, flipflop_8bit_1_p4, flipflop_8bit_1_p5,
       flipflop_8bit_1_p6, flipflop_8bit_1_p7, flipflop_8bit_1_p8, flipflop_8bit_2_y0, flipflop_8bit_2_y1,
       flipflop_8bit_2_y2, flipflop_8bit_2_y3, flipflop_8bit_2_y4, flipflop_8bit_2_y5, flipflop_8bit_2_y6,
       flipflop_8bit_2_y7, flipflop_8bit_3_y0, flipflop_8bit_3_y1, flipflop_8bit_3_y2, flipflop_8bit_3_y3,
       flipflop_8bit_3_y4, flipflop_8bit_3_y5, flipflop_8bit_3_y6, flipflop_8bit_3_y7, undriven, undriven_2,
       undriven_3, undriven_4, undriven_5, undriven_6, undriven_7, undriven_8;

  TriState_Switch tristate_switch_1 (
    .Y0(Y0), .Y1(Y1), .Y2(Y2), .Y3(Y3), .Y4(Y4), .Y5(Y5), .Y6(Y6), .Y7(Y7), .I0(I0), .I1(I1), .I2(I2),
    .I3(I3), .I4(I4), .I5(I5), .I6(I6), .I7(I7), .Enable(in_24));
  RAM_256B ram_256b_1 ();  // open: D0, D1, D2, D3, D4, D5, D6, D7, RAM_IN, RAM_OUT, CLK, S0, S1, S2, S3, S4, S5, S6, S7, Y0, Y1, Y2, Y3, Y4, Y5, Y6, Y7
  TriState_Switch tristate_switch_2 (
    .Y0(Y0), .Y1(Y1), .Y2(Y2), .Y3(Y3), .Y4(Y4), .Y5(Y5), .Y6(Y6), .Y7(Y7), .I0(flipflop_8bit_1_p1),
    .I1(flipflop_8bit_1_p2), .I2(flipflop_8bit_1_p3), .I3(flipflop_8bit_1_p4), .I4(flipflop_8bit_1_p5),
    .I5(flipflop_8bit_1_p6), .I6(flipflop_8bit_1_p7), .I7(flipflop_8bit_1_p8), .Enable(in_26));
  // Flipflop_8bit flipflop_8bit_1: pin names not known; wires that end beside it: flipflop_8bit_1_p1, flipflop_8bit_1_p2, flipflop_8bit_1_p3, flipflop_8bit_1_p4, flipflop_8bit_1_p5, flipflop_8bit_1_p6, flipflop_8bit_1_p7, flipflop_8bit_1_p8
  Flipflop_8bit flipflop_8bit_2 (
    .Y0(flipflop_8bit_2_y0), .Y1(flipflop_8bit_2_y1), .Y2(flipflop_8bit_2_y2), .Y3(flipflop_8bit_2_y3),
    .Y4(flipflop_8bit_2_y4), .Y5(flipflop_8bit_2_y5), .Y6(flipflop_8bit_2_y6), .Y7(flipflop_8bit_2_y7),
    .CLK(WRegA), .EN(1'b1), .D0(Y0), .D1(Y1), .D2(Y2), .D3(Y3), .D4(Y4), .D5(Y5), .D6(Y6), .D7(Y7));
  Flipflop_8bit flipflop_8bit_3 (
    .Y0(flipflop_8bit_3_y0), .Y1(flipflop_8bit_3_y1), .Y2(flipflop_8bit_3_y2), .Y3(flipflop_8bit_3_y3),
    .Y4(flipflop_8bit_3_y4), .Y5(flipflop_8bit_3_y5), .Y6(flipflop_8bit_3_y6), .Y7(flipflop_8bit_3_y7),
    .CLK(WRegB), .EN(1'b1), .D0(Y0), .D1(Y1), .D2(Y2), .D3(Y3), .D4(Y4), .D5(Y5), .D6(Y6), .D7(Y7));
  ALU alu_1 ();
  TriState_Switch tristate_switch_3 (
    .Y0(Y0), .Y1(Y1), .Y2(Y2), .Y3(Y3), .Y4(Y4), .Y5(Y5), .Y6(Y6), .Y7(Y7), .I0(undriven_8), .I1(undriven_7),
    .I2(undriven_5), .I3(undriven_6), .I4(undriven), .I5(undriven_2), .I6(undriven_3), .I7(undriven_4),
    .Enable(in_25));
endmodule
